# Fritzing sketch wiring (saved by Fritzing 1.0.8)
breadboards: 1

parts:
  부품1 = Arduino Uno (Rev3) - ICSP
  LCD1 = LCD1602 I2C
  R1 = Rotary Potentiometer (Small) [maximum_resistance=100kΩ knob_status=50% power=0.5W package=THT]  # not connected

nets:
  N1: 부품1.A4/SDA, LCD1.SDA
  N2: 부품1.A5/SCL, LCD1.SCL

custom parts:
  LCD1602 I2C: 16x2 character LCD with PCF8574 I2C backpack (GND, VCC, SDA, SCL)
